# Fritzing sketch AD9833_FG_Main_3V3_TA48033F_Test (saved by Fritzing 0.9.3b)
breadboards: 3

parts:
  U1 = atmega328 [package=dip]
  XTAL1 = Crystal [frequency="16 Mhz" package=THT]
  C1 = Ceramic Capacitor [capacitance=100nF package="100 mil [THT, multilayer]"]
  C2 = Ceramic Capacitor [capacitance=100nF package="100 mil [THT, multilayer]"]
  R1 = Resistor [tolerance=±5% resistance=10k package=THT]
  RE1 = Rotary Encoder [package=THT]
  S1 = Toggle Switch [package=THT]
  U2 = mystery part, 7 pins [chip_label="AD9833 Module"]
  C3 = Ceramic Capacitor [capacitance=100nF package="100 mil [THT, multilayer]"]
  C4 = Ceramic Capacitor [capacitance=100nF package="100 mil [THT, multilayer]"]
  U3 = mystery part, 9 pins [chip_label=SPLC792-I2C]
  U4 = Voltage Regulator - 3.3V [package="TO220 [THT]"]
  C5 = Electrolytic Capacitor [capacitance=1µF package="100 mil [THT, electrolytic]"]
  VCC1 = 4 x AAA Battery Mount
  R5 = Resistor [tolerance=±5% resistance=220 package=THT]
  R6 = Resistor [tolerance=±5% resistance=3.3k package=THT]
  IC1 = Dual Op-Amp [package=dip08]
  R8 = Rotary Potentiometer (Small) [maximum_resistance=100kΩ package=THT]
  R9 = Resistor [tolerance=±5% resistance=4.7k package=THT]
  R10 = Resistor [tolerance=±5% resistance=12. package=THT]
  C9 = Ceramic Capacitor [capacitance=100nF package="100 mil [THT, multilayer]"]
  C10 = Electrolytic Capacitor [capacitance=1µF package="100 mil [THT, electrolytic]"]
  R11 = Resistor [tolerance=±5% resistance=1k package=THT]
  C11 = Ceramic Capacitor [capacitance=100nF package="100 mil [THT, multilayer]"]
  R12 = Resistor [tolerance=±5% resistance=220 package=THT]
  LED1 = LED - 3mm [color="Green (560nm)" package="3 mm [THT]"]

nets:
  N1: U1.RESET, R1.Pin_0, RE1.EncoderPinA
  N2: U1.D3_(PWM), RE1.EncoderPinB
  N3: U1.D4, S1.L1
  N4: U1.VCC, U1.AVCC, R1.Pin_1, U2.pin2, C3.1, C4.0, U3.pin9, U4.output_voltage, C5.+, R12.Pin_1
  N5: U1.GND, C1.1, C2.0, RE1.EncoderPinC, S1.COM, S1.L2, U2.pin3, C3.0, C4.1, U3.pin2, U3.pin6, C5.-, VCC1.-, R6.Pin_1, IC1.A_V-, R8.leg1, R10.Pin_1, C9.0, C10.-, R11.Pin_1
  N6: U1.XLAT1, XTAL1.pin_1, C2.1
  N7: U1.XLAT2, XTAL1.pin_0, C1.0
  N8: U1.D10_(PWM), U2.pin6
  N9: U1.D11_(PWM), U2.pin4
  N10: U1.D13, U2.pin5
  N11: U1.A0, R5.Pin_1, R6.Pin_0
  N12: U1.A3, U3.pin3
  N13: U1.A4, U3.pin5
  N14: U1.A5, U3.pin4
  N15: U2.pin7, R8.leg2
  N16: U3.pin1, R12.Pin_0
  N17: U4.input_voltage, VCC1.+, R5.Pin_0, IC1.A_V+, C9.1, C10.+, C11.0, LED1.anode
  N18: U4.GND, C11.1
  N19: IC1.A_OUT, IC1.B_+IN, R9.Pin_0
  N20: IC1.A_-IN, R9.Pin_1, R10.Pin_0
  N21: IC1.A_+IN, R8.wiper
  N22: IC1.B_-IN, IC1.B_OUT
  N23: R11.Pin_0, LED1.cathode

notes:
  GND
  +3.3V
  OUT
  1.5V x 4
  GND
  +6V
  TA48033F
  1 IN
  2 GND
  3 OUT
  SPLC792-I2C
  1 VDD
  2 NC
  3 NC
  4 GND
  5 DATA
  6 CLK
  7 RESET
  8 GND
  9 BL+
  AD9833 Module
  1 REF
  2 VCC
  3 GND
  4 DAT
  5 CLK
  6 FUNC
  7 OUT
