# Fritzing sketch AD9833_FG_Test (saved by Fritzing 0.9.3b)
breadboards: 3

parts:
  パーツ1 = Arduino Uno (Rev3)
  U1 = mystery part, 9 pins [chip_label=SPLC792-I2C]
  R1 = Resistor [tolerance=±5% resistance=220 package=THT]
  R2 = Resistor [tolerance=±5% resistance=12k package=THT]
  R3 = Resistor [tolerance=±5% resistance=6.8k package=THT]
  RE1 = Rotary Encoder [package=THT]
  S1 = Pushbutton [package="[THT]"]
  C1 = Electrolytic Capacitor [capacitance=1µF package="100 mil [THT, electrolytic]"]
  U2 = mystery part, 7 pins [chip_label="AD8933 Unit"]
  C2 = Ceramic Capacitor [capacitance=100nF package="100 mil [THT, multilayer]"]
  IC1 = Dual Op-Amp [package=dip08]
  R4 = Resistor [tolerance=±5% resistance=220 package=THT]
  R5 = Resistor [tolerance=±5% resistance=220 package=THT]
  C3 = Ceramic Capacitor [capacitance=100nF package="100 mil [THT, multilayer]"]
  R6 = Rotary Potentiometer (Small) [maximum_resistance=100kΩ package=THT]

nets:
  N1: パーツ1.A3, R3.Pin_1
  N2: パーツ1.A4/SDA, U1.pin5
  N3: パーツ1.A5/SCL, U1.pin4
  N4: パーツ1.D10_PWM/SS, U2.pin6
  N5: パーツ1.D11_PWM/MOSI, U2.pin4
  N6: パーツ1.D13/SCK, U2.pin5
  N7: パーツ1.D2, RE1.EncoderPinA
  N8: パーツ1.D3_PWM, RE1.EncoderPinB
  N9: パーツ1.D4, S1.Pin_3, S1.Pin_4
  N10: パーツ1.3V3, U1.pin9, R1.Pin_0, C1.+
  N11: パーツ1.5V, U2.pin3, C2.1, IC1.A_V-, R5.Pin_0, C3.1, R6.leg1
  N12: パーツ1.GND, U1.pin2, U1.pin6, R2.Pin_0, RE1.EncoderPinC, S1.Pin_1, S1.Pin_2, C1.-
  N13: U1.pin1, R1.Pin_1
  N14: U1.pin3, R2.Pin_1, R3.Pin_0
  N15: U2.pin2, C2.0, IC1.A_V+, C3.0
  N16: U2.pin7, R6.leg2
  N17: IC1.A_OUT, IC1.B_+IN, R4.Pin_1
  N18: IC1.A_-IN, R4.Pin_0, R5.Pin_1
  N19: IC1.A_+IN, R6.wiper
  N20: IC1.B_-IN, IC1.B_OUT

notes:
  GND
  5V
  GND
  3.3V
  AD9833 Unit
  1 REF
  2 VCC
  3 GND
  4 DAT
  5 CLK
  6 FUNC
  7 OUT
  OUT
  10k/B
