# Fritzing sketch AD9833_FG_ケース内配線 (saved by Fritzing 0.9.3b)
perfboards: 2

parts:
  TRS1 = Audio Jack (TRS) 3.5mm [package="4Ucon 08780 [THT]"]  # not connected
  TRS2 = Audio Jack (TRS) 3.5mm [package="4Ucon 08780 [THT]"]  # not connected
  RE1 = Rotary Encoder [package=THT]  # not connected
  S1 = Toggle Switch [package=THT]
  R1 = Rotary Potentiometer (Small) [maximum_resistance=100kΩ package=THT]  # not connected
  VCC1 = 4 x AAA Battery Mount  # not connected
  S2 = Toggle Switch [package=THT]  # not connected

nets:
  N1: S1.COM, S1.L2

notes:
  Main Bard
  Amp Board
  PWR SW
  Freq RE
  WaveType SW
  Bypass Out
  Level
  Out
