# Fritzing sketch AD9833_UART_Test (saved by Fritzing 0.9.3b)
breadboards: 1

parts:
  U1 = mystery part, 7 pins [chip_label="AD9833 Unit"]
  パーツ1 = Arduino Uno (Rev3)

nets:
  N1: U1.pin2, パーツ1.5V
  N2: U1.pin3, パーツ1.GND
  N3: U1.pin4, パーツ1.D11_PWM/MOSI
  N4: U1.pin5, パーツ1.D13/SCK
  N5: U1.pin6, パーツ1.D10_PWM/SS

notes:
  AD9833 Unit
  1 REF
  2 VCC
  3 GND
  4 DAT
  5 CLK
  6 FUNC
  7 OUT
  GND
  5V
  OUT
