# Fritzing sketch Untitled Sketch (saved by Fritzing 0.9.3b)
breadboards: 1

parts:
  パーツ1 = Arduino Uno (Rev3)  # not connected
  U1 = mystery part, 9 pins [chip_label=SPLC792-I2C]
  R1 = Resistor [tolerance=±5% resistance=220 package=THT]
  R2 = Resistor [tolerance=±5% resistance=12k package=THT]
  R3 = Resistor [tolerance=±5% resistance=6.8k package=THT]
  RE1 = Rotary Encoder [package=THT]  # not connected

nets:
  N1: U1.pin1, R1.Pin_1
  N2: U1.pin2, U1.pin6, R2.Pin_0
  N3: U1.pin3, R2.Pin_1, R3.Pin_0
  N4: U1.pin9, R1.Pin_0
